// Digital circuit IPCS.dig as structural Verilog
module IPCS (
  input  [3:0] Schritt,
  input  C,
  input  [15:0] IP_in,
  input  [15:0] CS_in,
  input  [15:0] DB,
  output [15:0] IP_out,
  output [15:0] CS_out,
  output [19:0] Adr,
  output [15:0] TEST_IP_out
);

  wire decoder_1_out_0, decoder_1_out_4, decoder_1_out_5, decoder_1_out_6, decoder_1_out_7, decoder_1_out_8,
       delay_1_out, or_2_out, or_3_out, or_4_out, or_5_out, Step_4OR8;
  wire [15:0] driver_1_out, driver_2_out;
  wire [19:0] offsetadd_1_seg_plus_off;

  assign driver_1_out = decoder_1_out_0 ? IP_in : 16'bz;  // Driver driver_1
  assign driver_2_out = decoder_1_out_0 ? CS_in : 16'bz;  // Driver driver_2
  assign driver_1_out = Step_4OR8 ? DB : 16'bz;  // Driver driver_3
  assign driver_2_out = or_2_out ? DB : 16'bz;  // Driver driver_4
  or or_1 (Step_4OR8, decoder_1_out_4, decoder_1_out_8);
  or or_2 (or_2_out, decoder_1_out_5, decoder_1_out_7);
  Decoder #(.Selector_Bits(4)) decoder_1 (
    .sel(Schritt), .out_0(decoder_1_out_0), .out_4(decoder_1_out_4), .out_5(decoder_1_out_5),
    .out_6(decoder_1_out_6), .out_7(decoder_1_out_7), .out_8(decoder_1_out_8));  // open: out_1, out_2, out_3, out_9, out_10, out_11, out_12, out_13, out_14, out_15
  or or_3 (or_3_out, decoder_1_out_5, decoder_1_out_6);
  or or_4 (or_4_out, decoder_1_out_0, Step_4OR8);
  or or_5 (or_5_out, decoder_1_out_0, or_2_out);
  Register #(.Bits(16)) Save_IP_out (.D(driver_1_out), .C(C), .en(or_4_out), .Q(IP_out));
  Register #(.Bits(16)) Save_CS_out (.D(driver_2_out), .C(C), .en(or_5_out), .Q(CS_out));
  Delay delay_1 (.in(or_4_out), .out(delay_1_out));
  D_FF #(.Bits(16)) u_TEST_IP_out (.D(driver_1_out), .C(delay_1_out), .Q(TEST_IP_out));  // open: nQ
  Offsetadd offsetadd_1 (.Pointer(IP_out), .Segment(CS_out), .Seg_plus_Off(offsetadd_1_seg_plus_off));
  assign Adr = or_3_out ? offsetadd_1_seg_plus_off : 20'bz;  // Driver driver_5

  // Notes on the sheet:
  //   Schritt: Aktueller Schritt in der Simulation
  //   Adr: Fortsetzadresse (Adresse, an der die ISR steht)
  //   IP_in: default 45054
  //   CS_in: default 4660
  //   Step 4 OR 8: IP_out = DB
  //   Step 5 OR 7: CS_out = DB
  //   Step 0, 4 OR 8
  //   Step 0, 5 OR 7
  //   Delay needed to let 
  //   Databus signal propagate to D-input
  //   of D-Flipflop before Clock kicks
  //   Hold Adr on High-Z 
  //   until step 5
endmodule
