// Digital circuit Interruptcontroller.dig as structural Verilog
// Dieses Bauteil ist ein Interruptcontroller mit 8 Interrupt-Eingängen.
module Interruptcontroller (
  input  INTA,
  input  INT_0,
  input  INT_1,
  input  INT_2,
  input  INT_3,
  input  INT_4,
  input  INT_5,
  input  INT_6,
  input  INT_7,
  output INTR,
  output [15:0] DB,
  output _0,
  output _1,
  output _2,
  output _3,
  output _4,
  output _5,
  output _6,
  output _7,
  output EN
);

  wire decoder_1_out_0, Encoder_any;
  wire [2:0] Encoder_num, SAVE_INTR_Number_q;

  PriorityEncoder #(.Selector_Bits(3)) Encoder (
    .in0(INT_0), .in1(INT_1), .in2(INT_2), .in3(INT_3), .in4(INT_4), .in5(INT_5), .in6(INT_6), .in7(INT_7),
    .num(Encoder_num), .any(Encoder_any));
  // MIDI #(.midiInstrument("Xylophone"), .midiChannel(16)) Sound_when_Interrupt_was_selected: pin names not known; wires that end beside it: {Encoder_num, 4'b0000}, {7{1'b1}}, 1'b1, Encoder_any
  D_FF #(.Bits(3)) SAVE_INTR_Number (.D(Encoder_num), .C(Encoder_any), .Q(SAVE_INTR_Number_q));  // open: nQ
  RS_FF_AS SAVE_INTR (.S(Encoder_any), .R(~INTA), .Q(INTR));  // open: nQ
  RS_FF_AS SAVE_EN (.S(Encoder_any), .R(1'b0), .Q(EN));  // open: nQ
  Decoder #(.Selector_Bits(3)) decoder_1 (
    .sel(SAVE_INTR_Number_q), .out_0(decoder_1_out_0), .out_1(_1), .out_2(_2), .out_3(_3), .out_4(_4),
    .out_5(_5), .out_6(_6), .out_7(_7));
  assign DB = ~INTA ? {{13{1'b0}}, SAVE_INTR_Number_q} : 16'bz;  // DriverInvSel driverinvsel_1
  and and_1 (_0, EN, decoder_1_out_0);

  // Notes on the sheet:
  //   INTA: Ein aktives Interrupt-Acknowledge-Signal mit niedrigem Pegel (daher das '!') bestätigt die Annahme eines
  //   Hardware-Interrupts. Wird in Schritt 3 auf LOW gezogen., default 1
  //   DB: Datenbus
  //   INTA! is pulled low on Step 3
  //   Expand 3Bit INTR Number
  //   to 16Bit for Data Bus
  //   On Step 3: 
  //   Output INTR Number 
  //   to Data Bus
  //   AND so that 0 isn't put out when
  //   no Interrupt was selected yet
endmodule
