// Digital circuit Misc.dig as structural Verilog
// Dieses Bauteil dient nur der Optik. Es sorgt dafür, dass die LED am korrekten Schritt an ist und dafür, dass sich Daten auf Datenbus und Adressbus "langsam und in die richtige Richtung" fortbewegen.
module Misc (
  input  [15:0] DB,
  input  [19:0] AB,
  input  Next,
  input  Prev,
  input  [3:0] Schritt,
  input  _400Hz,
  input  Quiet,
  input  Louder,
  input  EN,
  output [15:0] D2,
  output [15:0] D4,
  output [15:0] D6,
  output [15:0] D8,
  output [15:0] D10,
  output [15:0] D22,
  output [15:0] D24,
  output [19:0] A6,
  output [19:0] A8,
  output [19:0] A10,
  output S9,
  output S8,
  output S7,
  output S6,
  output S5,
  output S4,
  output S3,
  output S2,
  output S1,
  output S0
);

  wire _0_78125Hz, _1_5625Hz, _3_125Hz, _6_25Hz, _12_5Hz, _25Hz, _50Hz, _100Hz, _200Hz, and_1_out, and_2_out,
       and_3_out, Clk_ISR, D0_S3, D0_S12, D0_S45, decoder_2_out_1, decoder_2_out_2, decoder_2_out_3,
       decoder_2_out_4, decoder_2_out_5, decoder_2_out_6, decoder_2_out_7, decoder_3_out_1, decoder_3_out_2,
       decoder_3_out_3, decoder_3_out_4, decoder_3_out_5, decoder_3_out_6, decoder_3_out_7, decoder_4_out_1,
       decoder_4_out_2, decoder_4_out_3, decoder_4_out_4, decoder_4_out_5, decoder_4_out_6, decoder_4_out_7,
       decoder_5_out_0, decoder_5_out_1, decoder_5_out_2, decoder_5_out_3, decoder_5_out_4, decoder_5_out_5,
       decoder_5_out_6, decoder_5_out_7, not_1_out, Only_allow_Louder_when_Volume_lt_0x70_lt,
       Only_allow_Quieter_when_Volume_gt_0_gt, or_1_out, or_2_out, or_3_out, or_4_out, or_5_out, or_6_out,
       or_7_out, or_8_out, or_9_out, or_10_out, or_11_out, Reset_ClkCounter;
  wire [2:0] Clock_Counter_2_out, Clock_counter_3_out, Clock_counter_out, Read_InterruptNr_in_Step_3_q;
  wire [3:0] step_counter_1_step;
  wire [6:0] Standard_Volume_is_middle_0x30_s;
  wire [7:0] mul_1_mul;

  or or_1 (or_1_out, S4, S5, S7, S8);
  or or_2 (or_2_out, S1, S2);
  or or_3 (or_3_out, Next, Prev);
  and and_1 (and_1_out, D0_S12, D0_S3, D0_S45);
  RS_FF_AS u_Reset_Clkcounter (.S(or_3_out), .R(and_1_out), .Q(Reset_ClkCounter));  // open: nQ
  assign D2 = or_4_out ? DB : 16'bz;  // Driver driver_1
  Counter #(.Bits(3)) Clock_counter (
    .en(or_1_out), .C(_0_78125Hz), .clr(Reset_ClkCounter), .out(Clock_counter_out));  // open: ovf
  Decoder #(.Selector_Bits(4)) decoder_1 (
    .sel(Schritt), .out_0(S0), .out_1(S1), .out_2(S2), .out_3(S3), .out_4(S4), .out_5(S5), .out_6(S6),
    .out_7(S7), .out_8(S8), .out_9(S9));  // open: out_10, out_11, out_12, out_13, out_14, out_15
  Counter #(.Bits(3)) Clock_Counter_2 (
    .en(S3), .C(_0_78125Hz), .clr(Reset_ClkCounter), .out(Clock_Counter_2_out));  // open: ovf
  assign D4 = or_4_out ? DB : 16'bz;  // Driver driver_2
  assign D6 = or_4_out ? DB : 16'bz;  // Driver driver_3
  assign A10 = or_6_out ? AB : 20'bz;  // Driver driver_4
  assign D22 = or_4_out ? DB : 16'bz;  // Driver driver_5
  assign D24 = or_4_out ? DB : 16'bz;  // Driver driver_6
  Counter #(.Bits(3)) Clock_counter_3 (
    .en(or_2_out), .C(_0_78125Hz), .clr(Reset_ClkCounter), .out(Clock_counter_3_out));  // open: ovf
  assign A6 = or_6_out ? AB : 20'bz;  // Driver driver_7
  assign A8 = or_6_out ? AB : 20'bz;  // Driver driver_8
  assign D2 = or_6_out ? DB : 16'bz;  // Driver driver_9
  assign D4 = decoder_4_out_4 ? DB : 16'bz;  // Driver driver_10
  assign D2 = decoder_4_out_4 ? DB : 16'bz;  // Driver driver_11
  or or_4 (or_4_out, decoder_2_out_5, decoder_2_out_6, decoder_2_out_7);
  assign D4 = or_6_out ? DB : 16'bz;  // Driver driver_12
  assign D6 = or_6_out ? DB : 16'bz;  // Driver driver_13
  assign D8 = decoder_4_out_4 ? DB : 16'bz;  // Driver driver_14
  assign D6 = decoder_4_out_4 ? DB : 16'bz;  // Driver driver_15
  Decoder #(.Selector_Bits(3)) decoder_2 (
    .sel(Clock_Counter_2_out), .out_0(D0_S3), .out_1(decoder_2_out_1), .out_2(decoder_2_out_2),
    .out_3(decoder_2_out_3), .out_4(decoder_2_out_4), .out_5(decoder_2_out_5), .out_6(decoder_2_out_6),
    .out_7(decoder_2_out_7));
  assign D6 = decoder_2_out_3 ? DB : 16'bz;  // Driver driver_16
  assign D4 = decoder_2_out_4 ? DB : 16'bz;  // Driver driver_17
  assign D8 = or_6_out ? DB : 16'bz;  // Driver driver_18
  assign D10 = or_6_out ? DB : 16'bz;  // Driver driver_19
  assign D22 = decoder_2_out_1 ? DB : 16'bz;  // Driver driver_20
  assign D24 = decoder_2_out_2 ? DB : 16'bz;  // Driver driver_21
  assign D24 = decoder_2_out_3 ? DB : 16'bz;  // Driver driver_22
  assign D6 = decoder_2_out_4 ? DB : 16'bz;  // Driver driver_23
  or or_5 (or_5_out, decoder_3_out_5, decoder_3_out_6, decoder_3_out_7);
  or or_6 (or_6_out, decoder_4_out_5, decoder_4_out_6, decoder_4_out_7);
  assign A8 = decoder_4_out_4 ? AB : 20'bz;  // Driver driver_24
  assign D22 = decoder_2_out_2 ? DB : 16'bz;  // Driver driver_25
  assign D24 = decoder_2_out_4 ? DB : 16'bz;  // Driver driver_26
  Decoder #(.Selector_Bits(3)) decoder_3 (
    .sel(Clock_counter_out), .out_0(D0_S45), .out_1(decoder_3_out_1), .out_2(decoder_3_out_2),
    .out_3(decoder_3_out_3), .out_4(decoder_3_out_4), .out_5(decoder_3_out_5), .out_6(decoder_3_out_6),
    .out_7(decoder_3_out_7));
  Decoder #(.Selector_Bits(3)) decoder_4 (
    .sel(Clock_counter_3_out), .out_0(D0_S12), .out_1(decoder_4_out_1), .out_2(decoder_4_out_2),
    .out_3(decoder_4_out_3), .out_4(decoder_4_out_4), .out_5(decoder_4_out_5), .out_6(decoder_4_out_6),
    .out_7(decoder_4_out_7));
  assign D2 = decoder_4_out_1 ? DB : 16'bz;  // Driver driver_27
  assign D4 = decoder_4_out_2 ? DB : 16'bz;  // Driver driver_28
  assign D4 = decoder_4_out_3 ? DB : 16'bz;  // Driver driver_29
  assign D6 = decoder_4_out_3 ? DB : 16'bz;  // Driver driver_30
  assign A6 = decoder_4_out_4 ? AB : 20'bz;  // Driver driver_31
  assign D22 = decoder_2_out_3 ? DB : 16'bz;  // Driver driver_32
  assign D22 = decoder_2_out_4 ? DB : 16'bz;  // Driver driver_33
  or or_7 (or_7_out, decoder_3_out_4, decoder_3_out_5, decoder_3_out_6, decoder_3_out_7);
  assign D2 = or_5_out ? DB : 16'bz;  // Driver driver_34
  assign D2 = decoder_4_out_2 ? DB : 16'bz;  // Driver driver_35
  assign D2 = decoder_4_out_3 ? DB : 16'bz;  // Driver driver_36
  assign A6 = decoder_4_out_3 ? AB : 20'bz;  // Driver driver_37
  assign D4 = or_7_out ? DB : 16'bz;  // Driver driver_38
  or or_8 (or_8_out, decoder_3_out_3, decoder_3_out_4, decoder_3_out_5, decoder_3_out_6, decoder_3_out_7);
  and and_2 (and_2_out, Only_allow_Louder_when_Volume_lt_0x70_lt, Louder);
  and and_3 (and_3_out, Quiet, Only_allow_Quieter_when_Volume_gt_0_gt);
  not not_1 (not_1_out, EN);
  Step_counter step_counter_1 (.Next(and_2_out), .Prev(and_3_out), .en(1'b1), .Step(step_counter_1_step));
  Counter #(.Bits(9)) Clock_Counter_4 (
    .en(1'b1), .C(_400Hz), .clr(1'b0),
    .out({_0_78125Hz, _1_5625Hz, _3_125Hz, _6_25Hz, _12_5Hz, _25Hz, _50Hz, _100Hz, _200Hz}));  // open: ovf
  assign D6 = or_8_out ? DB : 16'bz;  // Driver driver_39
  assign A6 = or_8_out ? AB : 20'bz;  // Driver driver_40
  or or_9 (or_9_out, S9, not_1_out);
  or or_10 (or_10_out, decoder_3_out_2, decoder_3_out_3, decoder_3_out_4, decoder_3_out_5, decoder_3_out_6, decoder_3_out_7);
  Mul #(.Bits(4)) mul_1 (.a(step_counter_1_step), .b(4'b1010), .mul(mul_1_mul));
  D_FF #(.Bits(3)) Read_InterruptNr_in_Step_3 (.D(DB[2:0]), .C(S3), .Q(Read_InterruptNr_in_Step_3_q));  // open: nQ
  assign Clk_ISR = decoder_5_out_4 ? _12_5Hz : 1'bz;  // Driver driver_41
  assign Clk_ISR = decoder_5_out_5 ? _50Hz : 1'bz;  // Driver driver_42
  assign D8 = or_10_out ? DB : 16'bz;  // Driver driver_43
  assign A8 = or_10_out ? AB : 20'bz;  // Driver driver_44
  assign Clk_ISR = decoder_5_out_6 ? _100Hz : 1'bz;  // Driver driver_45
  or or_11 (or_11_out, decoder_3_out_1, decoder_3_out_2, decoder_3_out_3, decoder_3_out_4, decoder_3_out_5, decoder_3_out_6, decoder_3_out_7);
  Comparator #(.Bits(7)) Only_allow_Louder_when_Volume_lt_0x70 (
    .a(Standard_Volume_is_middle_0x30_s), .b(7'b1110000), .lt(Only_allow_Louder_when_Volume_lt_0x70_lt));  // open: gt, eq
  Add #(.Bits(7)) Standard_Volume_is_middle_0x30 (
    .a(mul_1_mul[6:0]), .b(7'b0110000), .c_i(1'b0), .s(Standard_Volume_is_middle_0x30_s));  // open: c_o
  Comparator #(.Bits(7)) Only_allow_Quieter_when_Volume_gt_0 (
    .a(Standard_Volume_is_middle_0x30_s), .b({7{1'b0}}), .gt(Only_allow_Quieter_when_Volume_gt_0_gt));  // open: eq, lt
  assign Clk_ISR = decoder_5_out_7 ? _200Hz : 1'bz;  // Driver driver_46
  assign D10 = or_11_out ? DB : 16'bz;  // Driver driver_47
  assign A10 = or_11_out ? AB : 20'bz;  // Driver driver_48
  Decoder #(.Selector_Bits(3)) decoder_5 (
    .sel(Read_InterruptNr_in_Step_3_q), .out_0(decoder_5_out_0), .out_1(decoder_5_out_1),
    .out_2(decoder_5_out_2), .out_3(decoder_5_out_3), .out_4(decoder_5_out_4), .out_5(decoder_5_out_5),
    .out_6(decoder_5_out_6), .out_7(decoder_5_out_7));
  assign Clk_ISR = decoder_5_out_0 ? _1_5625Hz : 1'bz;  // Driver driver_49
  assign Clk_ISR = decoder_5_out_1 ? _3_125Hz : 1'bz;  // Driver driver_50
  BillieJean billiejean_1 (.C(_400Hz), .en(or_9_out), .Vol(Standard_Volume_is_middle_0x30_s));
  ISR isr_1 (.en(S6), .C(Clk_ISR), .Vol(Standard_Volume_is_middle_0x30_s));
  assign Clk_ISR = decoder_5_out_2 ? _3_125Hz : 1'bz;  // Driver driver_51
  assign Clk_ISR = decoder_5_out_3 ? _6_25Hz : 1'bz;  // Driver driver_52

  // Notes on the sheet:
  //   _400Hz: Hz: 400
  //   These two do the same thing.
  //   Lower design better!?
  //   Step 3: Output INTR Number to Data Bus
  //   Step 4&5: Aufnahme von IP & CS aus der Vektortabelle
  //   Step 7&8: POP CS & IP
  //   Step 1&2: PUSH IP & CS
  //   Clock Divider
  //   Set Clk_ISR
endmodule
