// Digital circuit Offsetadd.dig as structural Verilog
module Offsetadd (
  input  [15:0] Pointer,
  input  [15:0] Segment,
  output [19:0] Seg_plus_Off
);

  wire [19:0] barrelshifter_1_out;

  BarrelShifter #(.Bits(20)) barrelshifter_1 (.in({4'b0000, Segment}), .shift(5'b00100), .out(barrelshifter_1_out));
  Add #(.Bits(20)) add_1 (.a({4'b0000, Pointer}), .b(barrelshifter_1_out), .c_i(1'b0), .s(Seg_plus_Off));  // open: c_o

  // Notes on the sheet:
  //   Seg_plus_Off: Die Stack-Adresse entsteht durch Schieben des Stack-Segments (SS) um eine Stelle nach links (=Multiplikation mit 10hex) und anschließendes Addieren des Stack-Pointers (SP).
  //   Wenn beispielsweise das Stack-Segment (SS) die Adresse 1234hex und der Stack-Pointer die Adresse 5678hex enthält, dann ist die Stack-Adresse: 
  //   1234hex × 10hex + 5678hex = 
  //   12340hex + 5678hex = 
  //   179B8hex
  //   Pointer: Pointer
  //   Wird auf Segment, das um 4 Bit nach links geschoben wird, addiert
  //   Segment: Segment
  //   Wird um 4 Bit (eine Hex-Stelle) nach links geschoben und dann mit Pointer addiert
endmodule
