// Digital circuit Prozessor.dig as structural Verilog
// Dieses Bauteil ist eine Nachbildung der
// Interruptverarbeitungsfunktionen eines Intel 8086 Prozessors.
module Prozessor (
  input  C,
  input  [15:0] IP_In,
  input  [15:0] CS_In,
  input  [19:0] SAdr_In,
  input  [15:0] DB,
  input  Next,
  input  Prev,
  input  INTR,
  output [19:0] AB,
  output WR,
  output RD,
  output [15:0] IP_out,
  output [15:0] CS_Out,
  output [19:0] Adr_ISR,
  output [3:0] Schritt,
  output INTA,
  output [19:0] SAdr_Out
);

  wire _0, _1, _2, _3, _7, _8, decoder_1_out_4, decoder_1_out_5, decoder_1_out_10, or_1_out, or_2_out,
       or_3_out, Save_INTR_q;
  wire [19:0] add_1_s, driver_1_out, Save_InterruptNr_x4_on_Step_4_q, sub_1_s, sub_2_s;
  wire [31:0] InterruptNr_x4_mul;

  RS_FF_AS Save_INTR (.S(INTR), .R(1'b0), .Q(Save_INTR_q));  // open: nQ
  or or_1 (or_1_out, _0, _8);
  assign driver_1_out = or_1_out ? SAdr_In : 20'bz;  // Driver driver_1
  Step_counter step_counter_1 (.Next(Next), .Prev(Prev), .en(Save_INTR_q), .Step(Schritt));
  Mul #(.Bits(16)) InterruptNr_x4 (.a(DB), .b(16'h4), .mul(InterruptNr_x4_mul));
  IPCS ipcs_1 (
    .Schritt(Schritt), .C(C), .IP_in(IP_In), .CS_in(CS_In), .DB(DB), .IP_out(IP_out), .CS_out(CS_Out),
    .Adr(Adr_ISR));
  Sub #(.Bits(20)) sub_1 (.a(SAdr_In), .b(20'h2), .c_i(1'b0), .s(sub_1_s));  // open: c_o
  or or_2 (or_2_out, _1, _7);
  assign driver_1_out = or_2_out ? sub_1_s : 20'bz;  // Driver driver_2
  assign AB = _8 ? sub_1_s : 20'bz;  // Driver driver_3
  Stop stop_1 (.stop(decoder_1_out_10));
  assign DB = _2 ? CS_Out : 16'bz;  // Driver driver_4
  Register #(.Bits(20)) Save_InterruptNr_x4_on_Step_4 (
    .D(InterruptNr_x4_mul[19:0]), .C(C), .en(_3), .Q(Save_InterruptNr_x4_on_Step_4_q));
  Sub #(.Bits(20)) sub_2 (.a(sub_1_s), .b(20'h2), .c_i(1'b0), .s(sub_2_s));  // open: c_o
  assign driver_1_out = _2 ? sub_2_s : 20'bz;  // Driver driver_5
  Decoder #(.Selector_Bits(4)) decoder_1 (
    .sel(Schritt), .out_0(_0), .out_1(_1), .out_2(_2), .out_3(_3), .out_4(decoder_1_out_4),
    .out_5(decoder_1_out_5), .out_7(_7), .out_8(_8), .out_10(decoder_1_out_10));  // open: out_6, out_9, out_11, out_12, out_13, out_14, out_15
  assign AB = _7 ? sub_2_s : 20'bz;  // Driver driver_6
  assign DB = _1 ? IP_out : 16'bz;  // Driver driver_7
  Add #(.Bits(20)) add_1 (.a(Save_InterruptNr_x4_on_Step_4_q), .b(20'h2), .c_i(1'b0), .s(add_1_s));  // open: c_o
  assign AB = decoder_1_out_4 ? Save_InterruptNr_x4_on_Step_4_q : 20'bz;  // Driver driver_8
  assign AB = decoder_1_out_5 ? add_1_s : 20'bz;  // Driver driver_9
  assign AB = WR ? driver_1_out : 20'bz;  // Driver driver_10
  or or_3 (or_3_out, _0, WR, _7, _8);
  Register #(.Bits(20)) Save_SAdr_Out (.D(driver_1_out), .C(C), .en(or_3_out), .Q(SAdr_Out));
  or or_4 (WR, _1, _2);
  or or_5 (RD, decoder_1_out_4, decoder_1_out_5, _7, _8);
  not not_1 (INTA, _3);

  // Other names for the same wires on the sheet: _1_OR_2 = WR

  // Notes on the sheet:
  //   C: Hz: 400
  //   IP_In: default 4660
  //   CS_In: default 45054
  //   SAdr_In: Initiale Stack-Adresse
  //   Berechnet aus SS und SP, default 36
  //   AB: Adressbus
  //   DB: Datenbus
  //   Adr_ISR: Fortsetzadresse (Adresse, an der die ISR steht)
  //   Schritt: Aktueller Schritt in der Simulation
  //   Next: Go to next step
  //   Prev: Go to previous step
  //   INTR: Anschluss 18
  //   Dieser Interrupt-Anschluss wird nach dem Abschluss eines jeden Befehls abgetastet, um zu
  //   ermitteln, ob eine Interrupt-Anforderung durch einen Hardware-Baustein vorliegt. Die Abtastung kann durch ein gelöschtes Interrupt Flag verhindert (maskiert) werd
  //   SAdr_Out: AktuelleStack-Adresse
  //   Step 0 OR 8: 
  //   SAdr_Out = SAdr_In
  //   Step 1 OR 7: 
  //   SAdr_Out = SAdr_In - 0x2
  //   Step 2: DB = CS
  //   en is set to 3 to only output on Step 3
  //   later steps will use DB for RAM & IPCS
  //   and we don't want to interfere with that
  //   Step 8: AB = SAdr_In - 0x2
  //   Step 7: AB = SAdr_In - 0x4
  //   Step 2:
  //   SAdr_Out = SAdr_In - 0x4
  //   Step 1: DB = IP
  //   Step 4: AB = InterruptNr x4
  //   Step 5: AB = InterruptNr x4 + 2
  //   Step 1 OR 2: AB = SAdr_Out
endmodule
