// Digital circuit RAM_Control.dig as structural Verilog
// Dieses Bauteil dient zur Kontrolle des RAM-Bausteins.
module RAM_Control (
  input  C,
  input  [19:0] AB,
  input  WR,
  input  RD,
  input  [15:0] DB,
  input  [7:0] D,
  output [19:0] A
);

  wire and_1_out, and_2_out, and_3_out, and_4_out, decoder_1_out_4, decoder_1_out_5, decoder_1_out_6,
       decoder_1_out_7, delay_1_out, or_1_out, or_2_out;
  wire [2:0] Clock_Counter_out;
  wire [7:0] driver_3_out, driver_5_out;
  wire [15:0] register_1_q;
  wire [19:0] add_1_s;

  or or_1 (or_1_out, WR, RD);
  Counter #(.Bits(3)) Clock_Counter (.en(or_1_out), .C(C), .clr(~or_1_out), .out(Clock_Counter_out));  // open: ovf
  assign DB = RD ? register_1_q : 16'bz;  // Driver driver_1
  Register #(.Bits(8)) register_1 (.D(driver_3_out), .C(C), .en(and_1_out), .Q(register_1_q[7:0]));
  or or_2 (or_2_out, decoder_1_out_4, decoder_1_out_5, decoder_1_out_6, decoder_1_out_7);
  Decoder #(.Selector_Bits(3)) decoder_1 (
    .sel(Clock_Counter_out), .out_4(decoder_1_out_4), .out_5(decoder_1_out_5), .out_6(decoder_1_out_6),
    .out_7(decoder_1_out_7));  // open: out_0, out_1, out_2, out_3
  Add #(.Bits(20)) add_1 (.a(AB), .b(20'h1), .c_i(1'b0), .s(add_1_s));  // open: c_o
  and and_1 (and_1_out, ~or_2_out, RD);  // And
  and and_2 (and_2_out, ~or_2_out, WR);  // And
  Register #(.Bits(8)) register_2 (.D(driver_5_out), .C(C), .en(delay_1_out), .Q(register_1_q[15:8]));
  assign A = ~or_2_out ? AB : 20'bz;  // DriverInvSel driverinvsel_1
  assign D = and_2_out ? DB[7:0] : 8'bz;  // Driver driver_2
  assign driver_3_out = and_1_out ? D : 8'bz;  // Driver driver_3
  assign D = and_4_out ? DB[15:8] : 8'bz;  // Driver driver_4
  assign driver_5_out = delay_1_out ? D : 8'bz;  // Driver driver_5
  and and_3 (and_3_out, or_2_out, RD);
  assign A = or_2_out ? add_1_s : 20'bz;  // Driver driver_6
  and and_4 (and_4_out, or_2_out, WR);
  Delay delay_1 (.in(and_3_out), .out(delay_1_out));
  Delay delay_2 (.in(and_4_out));  // open: out

  // Notes on the sheet:
  //   For RD/WR high: Outputs high after 4 clock cycles
  //   Effectively delays RD/WR by 4 clock cycles
endmodule
