// Digital circuit INTRmulti.dig as structural Verilog
module INTRmulti (
  input  [15:0] DB,
  output [19:0] AB
);

  wire [39:20] mul_1_mul;

  Mul #(.Bits(20)) mul_1 (.a({{12{1'b0}}, DB[7:0]}), .b(20'h4), .mul({mul_1_mul, AB}));
endmodule
