// Digital circuit Interruptcontroller.dig as structural Verilog
// Dieses Bauteil ist ein Interruptcontroller mit 8 Interrupt-Eingängen.
module Interruptcontroller (
  input  INTA,
  input  C,
  input  INT_0,
  input  INT_1,
  input  INT_2,
  input  INT_3,
  input  INT_4,
  input  INT_5,
  input  INT_6,
  input  INT_7,
  output INT,
  output [7:0] DB,
  output _0,
  output _1,
  output _2,
  output _3,
  output _4,
  output _5,
  output _6,
  output _7,
  output EN
);

  wire and_1_out, and_2_out, d_ff_1_q, d_ff_2_q, d_ff_3_q, decoder_1_out_0, delay_1_out, delay_2_out,
       Encoder_any;
  wire [2:0] Encoder_num, register_1_q;

  PriorityEncoder #(.Selector_Bits(3)) Encoder (
    .in0(INT_0), .in1(INT_1), .in2(INT_2), .in3(INT_3), .in4(INT_4), .in5(INT_5), .in6(INT_6), .in7(INT_7),
    .num(Encoder_num), .any(Encoder_any));
  D_FF d_ff_1 (.D(INTA), .C(C), .Q(d_ff_1_q));  // open: nQ
  D_FF d_ff_2 (.D(Encoder_any), .C(C), .Q(d_ff_2_q));  // open: nQ
  Delay delay_1 (.in(d_ff_2_q), .out(delay_1_out));
  and and_1 (and_1_out, Encoder_any, d_ff_1_q);
  Delay #(.delayTime(2)) delay_2 (.in(C), .out(delay_2_out));
  and and_2 (and_2_out, d_ff_2_q, ~delay_1_out);  // And
  Register #(.Bits(3)) register_1 (.D(Encoder_num), .C(delay_2_out), .en(and_2_out), .Q(register_1_q));
  RS_FF rs_ff_1 (.S(and_1_out), .C(C), .R(~d_ff_1_q), .Q(INT));  // open: nQ
  assign DB = ~d_ff_1_q ? {{5{1'b0}}, register_1_q} : 8'bz;  // DriverInvSel driverinvsel_1
  D_FF d_ff_3 (.D(Encoder_any), .C(Encoder_any), .Q(d_ff_3_q));  // open: nQ
  Delay #(.delayTime(5)) delay_3 (.in(d_ff_3_q), .out(EN));
  Decoder #(.Selector_Bits(3)) decoder_1 (
    .sel(register_1_q), .out_0(decoder_1_out_0), .out_1(_1), .out_2(_2), .out_3(_3), .out_4(_4), .out_5(_5),
    .out_6(_6), .out_7(_7));
  and and_3 (_0, EN, decoder_1_out_0);

  // Notes on the sheet:
  //   INTA: default 1
  //   C: Hz: 10
endmodule
