// Digital circuit Offsetadd.dig as structural Verilog
module Offsetadd (
  input  [15:0] Pointer,
  input  [15:0] Segment,
  output [19:0] Seg_plus_Off
);

  wire [19:0] barrelshifter_1_out;

  BarrelShifter #(.Bits(20)) barrelshifter_1 (.in({4'b0000, Segment}), .shift(5'b00100), .out(barrelshifter_1_out));
  Add #(.Bits(20)) add_1 (.a({4'b0000, Pointer}), .b(barrelshifter_1_out), .c_i(1'b0), .s(Seg_plus_Off));  // open: c_o
endmodule
