// Digital circuit Prozessor.dig as structural Verilog
// Dieses Bauteil ist eine Nachbildung der
// Interruptverarbeitungsfunktionen eines Intel 8086 Prozessors.
module Prozessor (
  input  C,
  input  S,
  input  T,
  input  [15:0] IPi,
  input  [15:0] CSi,
  input  [15:0] SP,
  input  [15:0] SS,
  input  [15:0] DB,
  input  INTR,
  output [19:0] AB,
  output WR,
  output RD,
  output [15:0] IPo,
  output [15:0] CSo,
  output [19:0] Adr,
  output [19:0] SAdr,
  output INTA
);

  wire and_1_out, d_ff_1_q, decoder_1_out_1, decoder_1_out_2, decoder_1_out_3, decoder_1_out_4,
       decoder_1_out_5, decoder_1_out_7, delay_1_out, delay_2_out, delay_3_out, or_1_out;
  wire [2:0] counter_1_out;
  wire [15:0] driver_1_out, driver_2_out;
  wire [19:0] add_1_s, intrmulti_1_ab, register_1_q, sub_1_s;

  assign driver_1_out = or_1_out ? DB : 16'bz;  // Driver driver_1
  Counter #(.Bits(3)) counter_1 (.en(1'b1), .C(S), .clr(1'b0), .out(counter_1_out));  // open: ovf
  IPCS ipcs_1 (
    .IPin(IPi), .CSin(CSi), .S(counter_1_out), .C(C), .DB(driver_1_out), .IPout(IPo), .CSout(CSo), .Adr(Adr));
  Delay delay_1 (.in(T), .out(delay_1_out));
  Offsetadd offsetadd_1 (.Pointer(SP), .Segment(SS), .Seg_plus_Off(SAdr));
  assign driver_2_out = decoder_1_out_3 ? DB : 16'bz;  // Driver driver_2
  and and_1 (and_1_out, ~delay_1_out, T, decoder_1_out_7);  // And
  or or_1 (or_1_out, decoder_1_out_5, decoder_1_out_4);
  INTRmulti intrmulti_1 (.DB(driver_2_out), .AB(intrmulti_1_ab));
  Stop stop_1 (.stop(and_1_out));
  Sub #(.Bits(20)) sub_1 (.a(SAdr), .b(20'h2), .c_i(1'b0), .s(sub_1_s));  // open: c_o
  assign AB = decoder_1_out_1 ? SAdr : 20'bz;  // Driver driver_3
  Register #(.Bits(20)) register_1 (.D(intrmulti_1_ab), .C(C), .en(decoder_1_out_3), .Q(register_1_q));
  Decoder #(.Selector_Bits(3)) decoder_1 (
    .sel(counter_1_out), .out_1(decoder_1_out_1), .out_2(decoder_1_out_2), .out_3(decoder_1_out_3),
    .out_4(decoder_1_out_4), .out_5(decoder_1_out_5), .out_7(decoder_1_out_7));  // open: out_0, out_6
  assign AB = decoder_1_out_2 ? sub_1_s : 20'bz;  // Driver driver_4
  assign DB = decoder_1_out_1 ? IPo : 16'bz;  // Driver driver_5
  assign DB = decoder_1_out_2 ? CSo : 16'bz;  // Driver driver_6
  assign AB = decoder_1_out_4 ? register_1_q : 20'bz;  // Driver driver_7
  Add #(.Bits(20)) add_1 (.a(register_1_q), .b(20'h2), .c_i(1'b0), .s(add_1_s));  // open: c_o
  assign AB = decoder_1_out_5 ? add_1_s : 20'bz;  // Driver driver_8
  Delay #(.delayTime(10)) delay_2 (.in(decoder_1_out_4), .out(delay_2_out));
  D_FF d_ff_1 (.D(delay_2_out), .C(C), .Q(d_ff_1_q));  // open: nQ
  Delay #(.delayTime(10)) delay_3 (.in(d_ff_1_q), .out(delay_3_out));
  or or_2 (WR, decoder_1_out_1, decoder_1_out_2);
  or or_3 (RD, delay_3_out, decoder_1_out_5);
  not not_1 (INTA, decoder_1_out_3);

  // Notes on the sheet:
  //   C: Hz: 10
endmodule
