// Digital circuit Simulation_Hardware-Interruptverarbeitung_8086.dig as structural Verilog
module Simulation_Hardware_Interruptverarbeitung_8086 (
  input  [15:0] IP,
  input  [15:0] CS,
  input  [15:0] SP,
  input  [15:0] SS,
  input  Clock,
  input  T,
  output [15:0] IP_2,
  output [15:0] CS_2,
  output [19:0] Fortsetzadresse,
  output [19:0] Stack_Adresse,
  output [19:0] out_11,
  output [15:0] out_12
);

  wire _0, _1, _2, _3, _4, _5, _6, _7, EN, INT0_p1, INT1_p1, INT2_p1, INT3_p1, INT4_p1, INT5_p1, INT6_p1,
       INT7_p1, Interruptcontroller_int, Prozessor_inta, Prozessor_rd, Prozessor_wr, S;
  wire [7:0] RAM_d;
  wire [19:0] ram_control_1_a;

  LED INTR (.in(Interruptcontroller_int));
  LED INTA (.in(Prozessor_inta));
  // ButtonLED INT0: pin names not known; wires that end beside it: INT0_p1, _0
  // ButtonLED INT1: pin names not known; wires that end beside it: INT1_p1, _1
  // ButtonLED INT2: pin names not known; wires that end beside it: INT2_p1, _2
  // ButtonLED INT3: pin names not known; wires that end beside it: INT3_p1, _3
  // ButtonLED INT4: pin names not known; wires that end beside it: INT4_p1, _4
  // ButtonLED INT5: pin names not known; wires that end beside it: INT5_p1, _5
  // ButtonLED INT6: pin names not known; wires that end beside it: INT6_p1, _6
  // ButtonLED INT7: pin names not known; wires that end beside it: INT7_p1, _7
  Prozessor Prozessor (
    .C(Clock), .S(S), .T(T), .IPi(IP), .CSi(CS), .SP(SP), .SS(SS), .DB(out_12),
    .INTR(Interruptcontroller_int), .AB(out_11), .WR(Prozessor_wr), .RD(Prozessor_rd), .IPo(IP_2),
    .CSo(CS_2), .Adr(Fortsetzadresse), .SAdr(Stack_Adresse), .INTA(Prozessor_inta));
  Interruptcontroller Interruptcontroller (
    .INTA(Prozessor_inta), .C(Clock), .INT_0(INT0_p1), .INT_1(INT1_p1), .INT_2(INT2_p1), .INT_3(INT3_p1),
    .INT_4(INT4_p1), .INT_5(INT5_p1), .INT_6(INT6_p1), .INT_7(INT7_p1), .INT(Interruptcontroller_int),
    .DB(out_12[7:0]), ._0(_0), ._1(_1), ._2(_2), ._3(_3), ._4(_4), ._5(_5), ._6(_6), ._7(_7), .EN(EN));
  // ButtonLED buttonled_1: pin names not known; wires that end beside it: S, EN
  // NotConnected on out_12[15:8]
  LED Schreiben (.in(Prozessor_wr));
  LED Lesen (.in(Prozessor_rd));
  RAM_Control ram_control_1 (
    .C(Clock), .AB(out_11), .WR(Prozessor_wr), .RD(Prozessor_rd), .DB(out_12), .D(RAM_d), .A(ram_control_1_a));
  RAMSinglePort #(.AddrBits(20), .Bits(8)) RAM (
    .A(ram_control_1_a), .str(Prozessor_wr), .C(Clock), .ld(Prozessor_rd), .D(RAM_d));

  // Other names for the same wires on the sheet: Adr[19:0] = Fortsetzadresse; C = Clock; CSi[15:0] = CS;
  //   CSo[15:0] = CS_2; IPi[15:0] = IP; IPo[15:0] = IP_2; SAdr[19:0] = Stack_Adresse

  // Notes on the sheet:
  //   CS: default 57344
  //   SP: default 4094
  //   SS: default 24576
  //   Clock: Hz: 100
  //   -
  //   Hier Interrupt 
  //   auswählen
  //   Initialisierung der Registerinhalte
  //   Einzelschritt
  //   Einzelschrittmodus
  //   Das Anklicken des "Play-Symbols" im Kopfmenü startet die Simulation
  //   Zuerst Interrupt auswählen!
  //   Schritt 1: Register IP auf den Stack legen
  //   Schritt 2: Register CS auf den Stack legen
  //   Schritt 3: Aufnahme der Interruptnummer
  //   Schritt 4: Aufnahme von IP aus der Vektortabelle
  //   Schritt 5: Aufnahme von CS aus der Vektortabelle
  //   Schritt 6: Aufnahme der Fortsetzadresse abgeschlossen
  //   Schritt 7: Beendet die Simulation
  //   Simulation der Hardware-Interruptverarbeitung des Intel 8086 Prozessors
  //   Adressbus
  //   Datenbus
  //   Aktuelle Registerinhalte
  //   Durch Rechtsklick auf den Baustein "RAM", 
  //   kann der RAM ausgelesen und beschrieben werden. 
  //   Achtung der Speicherinhalt ist nur während der
  //   Simulation verfügbar!
  //   Adresse des Interruptprogramms
  //   Random Access Memory (RAM)
  //   Viel Spaß!
endmodule
